# Fritzing sketch MeeBleeps Freaq Schematic 08022022 (saved by Fritzing 0.9.9b)

parts:
  Audio_OUT = Audio Jack (TRS) 3.5mm [package="PG203J [THT]"]
  IC0 = Arduino Nano (Rev3.0)
  MIDI_Out = Audio Jack (TRS) 3.5mm [package="PG203J [THT]"]
  Sync_OUT = Audio Jack (TRS) 3.5mm [package="PG203J [THT]"]
  Sync_IN = Audio Jack (TRS) 3.5mm [package="PG203J [THT]"]
  S1 = Pushbutton [package=THT]
  S2 = Pushbutton [package=THT]
  S3 = Pushbutton [package=THT]
  S4 = Pushbutton [package=THT]
  R21 = Rotary Potentiometer (Small) [maximum_resistance=100kΩ package=THT]
  R22 = Rotary Potentiometer (Small) [maximum_resistance=100kΩ package=THT]
  R23 = Rotary Potentiometer (Small) [maximum_resistance=100kΩ package=THT]
  R24 = Rotary Potentiometer (Small) [maximum_resistance=100kΩ package=THT]
  R34 = Resistor [tolerance=±1% resistance=220 power=0.25 package=THT]
  R35 = Resistor [tolerance=±0.5% resistance=220 power=0.25 package=THT]
  Part1 = LED Matrix - Serial Interface - Red/Green/Blue
  S5 = Pushbutton [package=THT]
  S6 = Pushbutton [package=THT]
  R28 = Resistor [tolerance=±0.5% resistance=220 package="0805 [SMD]"]
  R29 = Rotary Potentiometer (Small) [maximum_resistance=100kΩ package=THT]
  R30 = Rotary Potentiometer (Small) [maximum_resistance=100kΩ package=THT]
  R31 = Rotary Potentiometer (Small) [maximum_resistance=100kΩ package=THT]
  R32 = Rotary Potentiometer (Small) [maximum_resistance=100kΩ package=THT]
  C1 = Electrolytic Capacitor [capacitance=0.1mF voltage=35V package="100 mil [THT, electrolytic]"]
  C2 = Ceramic Capacitor [capacitance=100nF voltage=35V package="100 mil [THT, multilayer]"]
  D1 = Rectifier Diode [part_number=1N4001 package="300 mil [THT]"]
  R33 = Resistor [tolerance=±0.5% resistance=10k package="0805 [SMD]"]
  C3 = Electrolytic Capacitor [capacitance=0.1mF voltage=35V package="100 mil [THT, electrolytic]"]
  C4 = Ceramic Capacitor [capacitance=100nF voltage=35V package="100 mil [THT, multilayer]"]
  C5 = Electrolytic Capacitor [capacitance=10µF voltage=35V package="100 mil [THT, electrolytic]"]

nets:
  GND: Audio_OUT.Sleeve, IC0.GND, MIDI_Out.Sleeve, Sync_OUT.Sleeve, Sync_IN.Sleeve, S1.leg1, S2.leg1, S3.leg1, S4.leg1, R21.leg1, R22.leg1, R23.leg1, R24.leg1, Part1.GND, S5.leg1, S6.leg1, R29.leg1, R30.leg1, R31.leg1, R32.leg1, C1.-, C2.0, R33.Pin_1, C3.-, C4.0, C5.-
  N1: Audio_OUT.Ring, R28.Pin_1, C2.1
  MIDI_OUT: IC0.D0/RX, R35.Pin_0
  SYNC_OUT: IC0.D2, Sync_OUT.Ring
  N2: IC0.D3, S6.leg0
  N3: IC0.D4, S5.leg0
  N4: IC0.D5, S4.leg0
  N5: IC0.D6, S3.leg0
  CS_LED: IC0.D7, Part1.CS
  SYNC_IN: IC0.D8, Sync_IN.Ring, R33.Pin_0
  PWM_AUDIO: IC0.D9, R28.Pin_0
  N6: IC0.D10, S2.leg0
  MOSI: IC0.D11/MOSI, Part1.MOSI
  N7: IC0.D12/MISO, S1.leg0
  N8: IC0.VIN, D1.cathode
  5V: IC0.5V, R21.leg2, R22.leg2, R23.leg2, R24.leg2, R34.Pin_0, Part1.VCC, R29.leg2, R30.leg2, R31.leg2, R32.leg2, C1.+, C5.+
  N9: IC0.A7, R31.wiper
  N10: IC0.A6, R32.wiper
  N11: IC0.A5, R29.wiper
  N12: IC0.A4, R30.wiper
  N13: IC0.A3, R24.wiper
  N14: IC0.A2, R23.wiper
  N15: IC0.A1, R22.wiper
  N16: IC0.A0, R21.wiper
  SCK: IC0.D13/SCK, Part1.SCK
  N17: MIDI_Out.Ring, R34.Pin_1
  N18: MIDI_Out.Tip, R35.Pin_1
  9V: D1.anode, C3.+, C4.1

notes:
  CV Out
  Optional MIDI Out (not included in final build)
